# Fritzing sketch scorepref (saved by Fritzing 0.9.1b)
stripboards: 1

parts:
  Part1 = Arduino Pro Mini v13
  IC1 = ULN2003A [package="SO16 [SMD]"]
  R3 = Resistor [tolerance=±5% resistance=330 package=THT]
  R4 = Resistor [tolerance=±5% resistance=330 package=THT]
  R5 = Resistor [tolerance=±5% resistance=330 package=THT]
  R6 = Resistor [tolerance=±5% resistance=330 package=THT]
  R7 = Resistor [tolerance=±5% resistance=330 package=THT]
  R8 = Resistor [tolerance=±5% resistance=330 package=THT]
  R2 = Resistor [tolerance=±5% resistance=330 package=THT]
  J1 = female pin header, 5 pins [form="♀ (female)"]
  J2 = female pin header, 5 pins [form="♀ (female)"]

nets:
  N1: Part1.D1/RX, R7.Pin_0, R7.Pin_1
  N2: Part1.D9_PWM, IC1.In_1
  N3: Part1.D8, IC1.In_2
  N4: Part1.D7, IC1.In_3
  N5: Part1.D6_PWM, IC1.In_4
  N6: Part1.D5_PWM, IC1.In_5
  N7: Part1.D4, IC1.In_6
  N8: Part1.D3_PWM, IC1.In_7
  N9: IC1.Out_4, R5.Pin_0
  N10: IC1.Out_3, R4.Pin_0
  N11: IC1.Out_2, R3.Pin_0
  N12: IC1.Out_1, R2.Pin_0
  N13: R3.Pin_1, J1.pin2, J2.pin2
  N14: R4.Pin_1, J1.pin4, J2.pin4
  N15: R5.Pin_1, J1.pin5, J2.pin5
  N16: R6.Pin_0, R6.Pin_1
  N17: R8.Pin_0, R8.Pin_1
  N18: R2.Pin_1, J1.pin1, J2.pin1
  N19: J1.pin3, J2.pin3
